// Logisim project lista7_exercicio1.circ as structural Verilog
module exe1 (
);

  wire A_q, A_qn, and_1_out, and_2_out, and_3_out, and_4_out, B_q, C_q, C_qn, clock_1_out, or_1_out;

  Clock clock_1 (.out(clock_1_out));
  J_K_Flip_Flop A (.J(and_2_out), .clk(clock_1_out), .K(A_q), .Q(A_q), .Qn(A_qn));  // open: preset, en, reset
  and and_1 (and_1_out, B_q, or_1_out);
  and and_2 (and_2_out, C_q, B_q);
  and and_3 (and_3_out, C_q, A_qn);
  J_K_Flip_Flop B (.J(and_3_out), .clk(clock_1_out), .K(and_1_out), .Q(B_q));  // open: Qn, preset, en, reset
  or or_1 (or_1_out, A_q, C_q);
  and and_4 (and_4_out, C_qn, A_qn);
  J_K_Flip_Flop C (.J(and_4_out), .clk(clock_1_out), .K(C_q), .Q(C_q), .Qn(C_qn));  // open: preset, en, reset
endmodule
